// Logisim project TallerLogica-Combinatorios.circ as structural Verilog: 9 circuits, main circuit sumador_simple
module sumador_simple (
  input  A,
  input  B,
  output S,
  output Cout
);

  xor xor_1 (S, A, B);
  and and_1 (Cout, A, B);
endmodule

module sumador_completo (
  input  Cin,
  input  A,
  input  B,
  output S,
  output Cout
);

  wire and_1_out, and_2_out, xor_1_out;

  xor xor_1 (xor_1_out, A, B);
  and and_1 (and_1_out, A, B);
  xor xor_2 (S, Cin, xor_1_out);
  and and_2 (and_2_out, xor_1_out, Cin);
  or or_1 (Cout, and_2_out, and_1_out);
endmodule

module sumador_4 (
  input  Cin,
  input  [3:0] A,
  input  [3:0] B,
  output [3:0] S,
  output Cout
);

  wire sumador_completo_1_cout, sumador_completo_2_cout, sumador_completo_3_cout;

  sumador_completo sumador_completo_1 (.Cin(Cin), .A(A[0]), .B(B[0]), .S(S[0]), .Cout(sumador_completo_1_cout));
  sumador_completo sumador_completo_2 (
    .Cin(sumador_completo_1_cout), .A(A[1]), .B(B[1]), .S(S[1]), .Cout(sumador_completo_2_cout));
  Hex_Digit_Display hex_digit_display_1 (.value(S));  // open: dp
  sumador_completo sumador_completo_3 (
    .Cin(sumador_completo_2_cout), .A(A[2]), .B(B[2]), .S(S[2]), .Cout(sumador_completo_3_cout));
  sumador_completo sumador_completo_4 (.Cin(sumador_completo_3_cout), .A(A[3]), .B(B[3]), .S(S[3]), .Cout(Cout));
endmodule

module comparador_cero (
  input  [3:0] A,
  output Z
);

  wire not_1_out, not_2_out, not_3_out, not_4_out;

  not not_1 (not_1_out, A[0]);
  not not_2 (not_2_out, A[2]);
  not not_3 (not_3_out, A[1]);
  not not_4 (not_4_out, A[3]);
  and and_1 (Z, not_1_out, not_2_out, not_3_out, not_4_out);
endmodule

module sumador_flags (
  input  Cin,
  input  [3:0] A,
  input  [3:0] B,
  output V,
  output [3:0] S,
  output N,
  output Z,
  output C
);

  wire and_1_out, not_1_out, not_2_out, sumador_4_1_cout, sumador_simple_1_cout, sumador_simple_2_cout,
       sumador_simple_3_cout, xor_1_out, xor_2_out;

  xor xor_1 (xor_1_out, A[3], B[3]);
  not not_1 (not_1_out, xor_1_out);
  sumador_simple sumador_simple_1 (.A(A[0]), .B(B[0]), .Cout(sumador_simple_1_cout));  // open: S
  sumador_simple sumador_simple_2 (.A(A[1]), .B(B[3]), .Cout(sumador_simple_2_cout));  // open: S
  sumador_simple sumador_simple_3 (.A(A[2]), .B(B[2]), .Cout(sumador_simple_3_cout));  // open: S
  sumador_4 sumador_4_1 (.Cin(Cin), .A(A), .B(B), .S(S), .Cout(sumador_4_1_cout));
  Hex_Digit_Display hex_digit_display_1 (.value(S));  // open: dp
  comparador_cero comparador_cero_1 (.A(S), .Z(Z));
  or or_1 (C, sumador_4_1_cout, sumador_simple_2_cout, sumador_simple_3_cout, sumador_simple_1_cout);
  and and_1 (and_1_out, Z, sumador_4_1_cout);
  xor xor_2 (xor_2_out, A[3], S[3]);
  and and_2 (V, not_1_out, xor_2_out);
  and and_3 (N, S[3], not_2_out);
  not not_2 (not_2_out, and_1_out);
endmodule

module incrementador_4 (
  input  [3:0] A,
  output [3:0] S
);

  Hex_Digit_Display hex_digit_display_1 (.value(S));  // open: dp
  sumador_4 sumador_4_1 (.A(A), .B(4'b0001), .S(S));  // open: Cin, Cout
endmodule

module inversor_4 (
  input  INV,
  input  [3:0] A,
  output [3:0] S
);

  wire [3:0] xor_1_out;

  xor xor_1 (xor_1_out[0], A[0], INV);
  xor xor_2 (xor_1_out[1], A[1], INV);
  xor xor_3 (xor_1_out[2], A[2], INV);
  xor xor_4 (xor_1_out[3], A[3], INV);
  incrementador_4 incrementador_4_1 (.A(xor_1_out), .S(S));
  Hex_Digit_Display hex_digit_display_1 (.value(S));  // open: dp
endmodule

module ALU (
  input  [1:0] OP,
  input  [3:0] A,
  input  [3:0] B,
  output N,
  output Z,
  output V,
  output C,
  output [3:0] S
);

  wire comparador_cero_1_z, comparador_cero_2_z, not_1_out, sumador_flags_1_p4, sumador_flags_1_p5,
       sumador_flags_1_p6, sumador_flags_1_p7, sumador_flags_2_p5, sumador_flags_2_p6, sumador_flags_2_p7,
       sumador_flags_2_p8;
  wire [3:0] and_1_out, inversor_4_1_s, or_1_out, sumador_flags_1_p3, sumador_flags_2_p4;

  and and_1 (and_1_out[0], A[0], B[0]);
  and and_2 (and_1_out[1], A[1], B[1]);
  and and_3 (and_1_out[2], A[2], B[2]);
  and and_4 (and_1_out[3], A[3], B[3]);
  or or_1 (or_1_out[0], A[0], B[0]);
  or or_2 (or_1_out[1], A[1], B[1]);
  or or_3 (or_1_out[2], A[2], B[2]);
  or or_4 (or_1_out[3], A[3], B[3]);
  // sumador_flags sumador_flags_1: pin names not known; wires that end beside it: A, B, sumador_flags_1_p3, sumador_flags_1_p4, sumador_flags_1_p5, sumador_flags_1_p6, sumador_flags_1_p7
  inversor_4 inversor_4_1 (.INV(1'b1), .A(B), .S(inversor_4_1_s));
  // sumador_flags sumador_flags_2: pin names not known; wires that end beside it: 1'b1, A, inversor_4_1_s, sumador_flags_2_p4, sumador_flags_2_p5, sumador_flags_2_p6, sumador_flags_2_p7, sumador_flags_2_p8
  not not_1 (not_1_out, sumador_flags_2_p8);
  comparador_cero comparador_cero_1 (.A(and_1_out), .Z(comparador_cero_1_z));
  comparador_cero comparador_cero_2 (.A(or_1_out), .Z(comparador_cero_2_z));
  Multiplexer #(.select(2)) multiplexer_1 (
    .in0(sumador_flags_1_p4), .in1(sumador_flags_2_p5), .in2(and_1_out[3]), .in3(or_1_out[3]), .out(N),
    .sel(OP));
  Multiplexer #(.select(2)) multiplexer_2 (
    .in0(sumador_flags_1_p5), .in1(sumador_flags_2_p6), .in2(comparador_cero_1_z), .in3(comparador_cero_2_z),
    .out(Z), .sel(OP));
  Multiplexer #(.select(2)) multiplexer_3 (
    .in0(sumador_flags_1_p6), .in1(sumador_flags_2_p7), .in2(1'b0), .in3(1'b0), .out(V), .sel(OP));
  Multiplexer #(.select(2)) multiplexer_4 (
    .in0(sumador_flags_1_p7), .in1(not_1_out), .in2(1'b0), .in3(1'b0), .out(C), .sel(OP));
  Multiplexer #(.select(2), .width(4)) multiplexer_5 (
    .in0(sumador_flags_1_p3), .in1(sumador_flags_2_p4), .in2(and_1_out), .in3(or_1_out), .out(S), .sel(OP));
  Hex_Digit_Display hex_digit_display_1 (.value(S));  // open: dp
endmodule

module verificador (
  output [3:0] out_1,
  output [3:0] out_2,
  output [1:0] out_3,
  output halt,
  output N,
  output Z,
  output V,
  output C,
  output [3:0] res
);

  wire clock_1_out;

  Clock clock_1 (.out(clock_1_out));
  Counter #(.max('h3ff), .width(10)) counter_1 (
    .clk(clock_1_out), .carry(halt), .Q({out_3, out_2, out_1}));  // open: clr, load, up, count, D
  // ALU alu_1: pin names not known; wires that end beside it: out_1, out_2, out_3, N, Z, V, C, res
endmodule
