// Logisim project TallerLogica-Secuenciales.circ as structural Verilog: 6 circuits, main circuit buffer_tres_estados
module buffer_tres_estados (
  input  A,
  input  A_en,
  input  B,
  input  B_en,
  input  C,
  input  C_en,
  output Res
);

  assign Res = A_en ? A : 1'bz;  // Controlled_Buffer controlled_buffer_1
  assign Res = B_en ? B : 1'bz;  // Controlled_Buffer controlled_buffer_2
  assign Res = C_en ? C : 1'bz;  // Controlled_Buffer controlled_buffer_3
endmodule

module registro_salida_restringida (
  input  clk,
  input  Reg_in,
  input  en_out,
  input  w,
  output Reg_Debug,
  output Reg_output
);

  wire and_1_out, and_2_out, not_1_out, or_1_out;

  and and_1 (and_1_out, Reg_in, w);
  or or_1 (or_1_out, and_1_out, and_2_out);
  and and_2 (and_2_out, not_1_out, Reg_Debug);
  not not_1 (not_1_out, w);
  D_Flip_Flop d_ff_1 (.D(or_1_out), .clk(clk), .Q(Reg_Debug));  // open: Qn, preset, reset
  assign Reg_output = en_out ? Reg_Debug : 1'bz;  // Controlled_Buffer controlled_buffer_1
endmodule

module registro_4bytes_salida (
  input  clk,
  input  [3:0] Reg4_in,
  input  en_out,
  input  w,
  output [3:0] Reg4_Debug,
  output [3:0] Reg4_output
);

  registro_salida_restringida registro_salida_restringida_1 (
    .clk(clk), .Reg_in(Reg4_in[0]), .en_out(en_out), .w(w), .Reg_Debug(Reg4_Debug[0]),
    .Reg_output(Reg4_output[0]));
  registro_salida_restringida registro_salida_restringida_2 (
    .clk(clk), .Reg_in(Reg4_in[1]), .en_out(en_out), .w(w), .Reg_Debug(Reg4_Debug[1]),
    .Reg_output(Reg4_output[1]));
  registro_salida_restringida registro_salida_restringida_3 (
    .clk(clk), .Reg_in(Reg4_in[2]), .en_out(en_out), .w(w), .Reg_Debug(Reg4_Debug[2]),
    .Reg_output(Reg4_output[2]));
  registro_salida_restringida registro_salida_restringida_4 (
    .clk(clk), .Reg_in(Reg4_in[3]), .en_out(en_out), .w(w), .Reg_Debug(Reg4_Debug[3]),
    .Reg_output(Reg4_output[3]));
endmodule

module ALU_regs (
  input  clk,
  input  [3:0] A,
  input  A_Write,
  input  in_4,
  input  [3:0] B,
  input  B_Write,
  input  [1:0] OP,
  output [3:0] A_Debug,
  output [3:0] B_Debug,
  output [3:0] S_Debug,
  output N,
  output [3:0] Reg4_output,
  output Z,
  output V,
  output C
);

  wire not_1_out;
  wire [3:0] alu_1_p8, registro_4bytes_salida_1_reg4_output, registro_4bytes_salida_2_reg4_output;

  Hex_Digit_Display hex_digit_display_1 (.value(A_Debug));  // open: dp
  registro_4bytes_salida registro_4bytes_salida_1 (
    .clk(clk), .Reg4_in(A), .en_out(A_Write), .w(1'b1), .Reg4_Debug(A_Debug),
    .Reg4_output(registro_4bytes_salida_1_reg4_output));
  registro_4bytes_salida registro_4bytes_salida_2 (
    .clk(clk), .Reg4_in(B), .en_out(B_Write), .w(1'b1), .Reg4_Debug(B_Debug),
    .Reg4_output(registro_4bytes_salida_2_reg4_output));
  Hex_Digit_Display hex_digit_display_2 (.value(B_Debug));  // open: dp
  // ALU alu_1: pin names not known; wires that end beside it: registro_4bytes_salida_1_reg4_output, registro_4bytes_salida_2_reg4_output, OP, N, Z, V, C, alu_1_p8
  not not_1 (not_1_out, clk);
  Hex_Digit_Display hex_digit_display_3 (.value(S_Debug));  // open: dp
  registro_4bytes_salida registro_4bytes_salida_3 (
    .clk(not_1_out), .Reg4_in(alu_1_p8), .en_out(1'b1), .w(in_4), .Reg4_Debug(S_Debug),
    .Reg4_output(Reg4_output));
endmodule

module ej_02 (
  input  in_1,
  input  in_2,
  input  in_3,
  input  in_4,
  input  clk,
  input  Force_Input,
  input  in_7,
  input  in_8,
  input  en_Force_Input,
  output R0,
  output out_11,
  output R1,
  output R2
);

  assign out_11 = en_Force_Input ? Force_Input : 1'bz;  // Controlled_Buffer controlled_buffer_1
  registro_salida_restringida registro_salida_restringida_1 (
    .clk(clk), .Reg_in(out_11), .en_out(in_1), .w(in_2), .Reg_Debug(R0), .Reg_output(out_11));
  registro_salida_restringida registro_salida_restringida_2 (
    .clk(clk), .Reg_in(out_11), .en_out(in_3), .w(in_4), .Reg_Debug(R1), .Reg_output(out_11));
  registro_salida_restringida registro_salida_restringida_3 (
    .clk(clk), .Reg_in(out_11), .en_out(in_7), .w(in_8), .Reg_Debug(R2), .Reg_output(out_11));
endmodule

module ej_03 (
  input  clk,
  input  ALU_A_Write,
  input  ALU_B_Write,
  input  [1:0] OP,
  input  ALU_enableOut,
  input  Reg0_Write,
  input  Reg0_enableOut,
  input  Reg1_Write,
  input  Reg1_enableOut,
  input  Reg2_Write,
  input  Reg2_enableOut,
  input  Reg3_Write,
  input  Reg3_enableOut,
  input  [3:0] Force_Input,
  input  en_Force_Input,
  output N,
  output Z,
  output V,
  output C
);

  wire [3:0] alu_regs_1_a_debug, alu_regs_1_b_debug, alu_regs_1_s_debug, controlled_buffer_1_out,
       Registro_00_reg4_debug, Registro_00_reg4_output, Registro_01_reg4_debug, Registro_02_reg4_debug,
       Registro_03_reg4_debug;

  assign controlled_buffer_1_out = en_Force_Input ? Force_Input : 4'bz;  // Controlled_Buffer controlled_buffer_1
  registro_4bytes_salida Registro_00 (
    .clk(clk), .Reg4_in(controlled_buffer_1_out), .en_out(Reg0_Write), .w(Reg0_enableOut),
    .Reg4_Debug(Registro_00_reg4_debug), .Reg4_output(Registro_00_reg4_output));
  registro_4bytes_salida Registro_01 (
    .clk(clk), .Reg4_in(controlled_buffer_1_out), .en_out(Reg1_Write), .w(Reg1_enableOut),
    .Reg4_Debug(Registro_01_reg4_debug), .Reg4_output(Registro_00_reg4_output));
  registro_4bytes_salida Registro_02 (
    .clk(clk), .Reg4_in(controlled_buffer_1_out), .en_out(Reg2_Write), .w(Reg2_enableOut),
    .Reg4_Debug(Registro_02_reg4_debug), .Reg4_output(Registro_00_reg4_output));
  registro_4bytes_salida Registro_03 (
    .clk(clk), .Reg4_in(controlled_buffer_1_out), .en_out(Reg3_Write), .w(Reg3_enableOut),
    .Reg4_Debug(Registro_03_reg4_debug), .Reg4_output(Registro_00_reg4_output));
  Hex_Digit_Display hex_digit_display_1 (.value(Registro_00_reg4_debug));  // open: dp
  Hex_Digit_Display hex_digit_display_2 (.value(Registro_01_reg4_debug));  // open: dp
  Hex_Digit_Display hex_digit_display_3 (.value(Registro_02_reg4_debug));  // open: dp
  Hex_Digit_Display hex_digit_display_4 (.value(Registro_03_reg4_debug));  // open: dp
  Hex_Digit_Display hex_digit_display_5 (.value(alu_regs_1_a_debug));  // open: dp
  Hex_Digit_Display Bus_2 (.value(controlled_buffer_1_out));  // open: dp
  Hex_Digit_Display hex_digit_display_6 (.value(alu_regs_1_b_debug));  // open: dp
  ALU_regs alu_regs_1 (
    .in_4(ALU_enableOut), .A_Write(ALU_A_Write), .B_Write(ALU_B_Write), .clk(clk),
    .A(Registro_00_reg4_output), .B(Registro_00_reg4_output), .OP(OP), .S_Debug(alu_regs_1_s_debug),
    .Reg4_output(controlled_buffer_1_out), .A_Debug(alu_regs_1_a_debug), .B_Debug(alu_regs_1_b_debug), .N(N),
    .Z(Z), .V(V), .C(C));
  Hex_Digit_Display hex_digit_display_7 (.value(alu_regs_1_s_debug));  // open: dp
endmodule
